// Logisim project trab.circ as structural Verilog: 1 circuit, main circuit main
module main (
  input  [1:0] _2,
  input  in_2,
  input  [7:0] in_3,
  input  in_4,
  input  [1:0] _1,
  input  Reset_Counter,
  input  [1:0] _0,
  output out_8
);

  wire clock_1_out, not_1_out;
  wire [1:0] bitselector_1_out, bitselector_2_out, bitselector_3_out;
  wire [5:0] rom_1_data;
  wire [7:0] \Percorre_a_Memória_q ;

  Counter #(.ongoal("stay")) \Percorre_a_Memória  (
    .load(in_2), .D(in_3), .count(in_4), .Q(\Percorre_a_Memória_q ), .carry(out_8), .clk(clock_1_out),
    .clr(Reset_Counter));
  Clock clock_1 (.out(clock_1_out));
  not not_1 (not_1_out, out_8);
  ROM #(.dataWidth(6)) rom_1 (.addr(\Percorre_a_Memória_q ), .data(rom_1_data), .sel(not_1_out));
  BitSelector #(.width(6), .group(2)) bitselector_1 (.in(rom_1_data), .out(bitselector_1_out), .sel(_2));
  BitSelector #(.width(6), .group(2)) bitselector_2 (.in(rom_1_data), .out(bitselector_2_out), .sel(_1));
  BitSelector #(.width(6), .group(2)) bitselector_3 (.in(rom_1_data), .out(bitselector_3_out), .sel(_0));
  DotMatrix #(.inputtype("row"), .matrixcols(2), .matrixrows(3), .dotshape("circle")) dotmatrix_1 (
    .row0(bitselector_1_out), .row1(bitselector_2_out), .row2(bitselector_3_out));

  // Notes on the sheet:
  //   ROM
endmodule
